# Fritzing sketch NewLaser Beam Break Security Alarm  (saved by Fritzing 0.8.7b)

parts:
  Part1 = Arduino Uno (Rev3)
  Mod1 = KY-008 Laser Transmitter Module [package="Breakout board"]
  VCC1 = 4 x AAA Battery Mount
  J1 = Piezo Speaker
  R1 = Resistor [tolerance=±5% resistance=220 package=THT]
  LED1 = LED - 5mm [color="Red (633nm)" package="5 mm [THT]"]
  R3 = Resistor [tolerance=±5% resistance=10k package=THT]
  R4 = Photocell (LDR) [package=THT]

nets:
  N1: Part1.A0, R3.Pin_0, R4.pin_0
  N2: Part1.D8, R1.Pin_1
  N3: Part1.GND, J1.pin1, LED1.cathode, R3.Pin_1
  N4: Part1.D7, J1.pin2
  N5: Part1.5V, R4.pin_1
  N6: Mod1.S, VCC1.+
  N7: Mod1.-, VCC1.-
  N8: R1.Pin_0, LED1.anode

custom parts:
  KY-008 Laser Transmitter Module: KY-008 Laser Transmitter Module, emits a dot shaped red laser beam.
